// Logisim project control_logic.circ as structural Verilog: 1 circuit, main circuit control_logic
module control_logic (
  input  [31:0] inst,
  input  BrEq,
  input  BrLt,
  output PCSel,
  output RegWEn,
  output [2:0] ImmSel,
  output BrUn,
  output ASel,
  output BSel,
  output [3:0] ALUSel,
  output MemRW,
  output [1:0] WBSel,
  output CSRSel,
  output CSRWen
);

  wire and_1_out, and_2_out, and_3_out, and_4_out, and_11_out, comparator_6_eq, comparator_7_eq,
       comparator_8_eq, comparator_9_eq, comparator_10_eq, comparator_11_eq, comparator_12_eq,
       comparator_13_gt, comparator_14_eq, comparator_15_gt, comparator_16_eq, comparator_17_gt,
       comparator_18_eq, comparator_19_eq, comparator_20_eq, comparator_21_eq, comparator_22_eq,
       comparator_23_eq, is_auipc, is_B_type, is_bgeu, is_bltu, is_I_type, is_J_type, is_jalr, is_load_inst,
       is_lui, is_mul, is_mulh, is_R_type, is_sra_or_srai, is_sub, is_U_type, not_1_out, not_2_out, or_1_out,
       or_2_out, or_3_out, or_5_out, or_7_out, or_8_out;
  wire [1:0] multiplexer_8_out;
  wire [2:0] multiplexer_1_out, multiplexer_2_out, multiplexer_4_out, multiplexer_6_out;
  wire [3:0] multiplexer_3_out, multiplexer_5_out, multiplexer_7_out, multiplexer_10_out, multiplexer_11_out;

  Multiplexer #(.enable("false"), .width(3)) multiplexer_1 (
    .in0(3'b000), .in1(3'b001), .out(multiplexer_1_out), .sel(MemRW));
  Comparator #(.width(7)) comparator_1 (.a(inst[6:0]), .b(7'b0110011), .eq(is_R_type));  // open: gt, lt
  Comparator #(.width(7)) comparator_2 (.a(inst[6:0]), .b(7'b0000011), .eq(is_load_inst));  // open: gt, lt
  Comparator #(.width(7)) comparator_3 (.a(inst[6:0]), .b(7'b0010011), .eq(is_I_type));  // open: gt, lt
  Comparator #(.width(7)) comparator_4 (.a(inst[6:0]), .b(7'b0100011), .eq(MemRW));  // open: gt, lt
  Comparator #(.width(7)) comparator_5 (.a(inst[6:0]), .b(7'b1100011), .eq(is_B_type));  // open: gt, lt
  Comparator #(.width(3)) comparator_6 (.a(inst[14:12]), .b(3'b110), .eq(comparator_6_eq));  // open: gt, lt
  Comparator #(.width(3)) comparator_7 (.a(inst[14:12]), .b(3'b100), .eq(comparator_7_eq));  // open: gt, lt
  Comparator #(.width(3)) comparator_8 (.a(inst[14:12]), .b(3'b101), .eq(comparator_8_eq));  // open: gt, lt
  Comparator #(.width(3)) comparator_9 (.a(inst[14:12]), .b(3'b111), .eq(comparator_9_eq));  // open: gt, lt
  Comparator #(.width(3)) comparator_10 (.a(inst[14:12]), .b(3'b000), .eq(comparator_10_eq));  // open: gt, lt
  Comparator #(.width(3)) comparator_11 (.a(inst[14:12]), .b(3'b001), .eq(comparator_11_eq));  // open: gt, lt
  not not_1 (not_1_out, BrEq);
  or or_1 (or_1_out, comparator_6_eq, comparator_7_eq);
  or or_2 (or_2_out, comparator_8_eq, comparator_9_eq);
  not not_2 (not_2_out, BrLt);
  Multiplexer #(.enable("false"), .width(3)) multiplexer_2 (
    .in0(multiplexer_1_out), .in1(3'b010), .out(multiplexer_2_out), .sel(is_B_type));
  Comparator #(.width(3)) comparator_12 (.a(inst[14:12]), .b(3'b000), .eq(comparator_12_eq));  // open: gt, lt
  Comparator #(.width(7)) comparator_13 (.a(7'b0100000), .b(inst[31:25]), .gt(comparator_13_gt));  // open: eq, lt
  Comparator #(.width(3)) comparator_14 (.a(inst[14:12]), .b(3'b000), .eq(comparator_14_eq));  // open: gt, lt
  Comparator #(.width(7)) comparator_15 (.a(7'b0000001), .b(inst[31:25]), .gt(comparator_15_gt));  // open: eq, lt
  Comparator #(.width(3)) comparator_16 (.a(inst[14:12]), .b(3'b001), .eq(comparator_16_eq));  // open: gt, lt
  Comparator #(.width(7)) comparator_17 (.a(7'b0000001), .gt(comparator_17_gt));  // open: b, eq, lt
  Multiplexer #(.enable("false"), .select(3), .width(4)) multiplexer_3 (
    .in0(4'b0000), .in1(4'b0110), .in2(4'b0111), .in3(4'b1011), .in4(4'b0011), .in5(4'b0100), .in6(4'b0010),
    .in7(4'b0001), .out(multiplexer_3_out), .sel(inst[14:12]));
  Comparator #(.width(3)) comparator_18 (.a(inst[14:12]), .b(3'b110), .eq(comparator_18_eq));  // open: gt, lt
  Comparator #(.width(3)) comparator_19 (.a(inst[14:12]), .b(3'b111), .eq(comparator_19_eq));  // open: gt, lt
  and and_1 (and_1_out, comparator_10_eq, BrEq);
  and and_2 (and_2_out, comparator_11_eq, not_1_out);
  and and_3 (and_3_out, or_1_out, BrLt);
  and and_4 (and_4_out, or_2_out, not_2_out);
  Multiplexer #(.enable("false"), .width(3)) multiplexer_4 (
    .in0(multiplexer_2_out), .in1(3'b011), .out(multiplexer_4_out), .sel(is_U_type));
  and and_5 (is_sub, comparator_12_eq, is_R_type, comparator_13_gt);
  and and_6 (is_mul, comparator_14_eq, is_R_type, comparator_15_gt);
  and and_7 (is_mulh, comparator_16_eq, is_R_type, comparator_17_gt);
  Multiplexer #(.enable("false"), .width(4)) multiplexer_5 (
    .in0(multiplexer_3_out), .in1(4'b1100), .out(multiplexer_5_out), .sel(is_sub));
  and and_8 (is_bltu, comparator_18_eq, is_B_type);
  and and_9 (is_bgeu, comparator_19_eq, is_B_type);
  or or_3 (or_3_out, and_1_out, and_2_out, and_3_out, and_4_out);
  Multiplexer #(.enable("false"), .width(3)) multiplexer_6 (
    .in0(multiplexer_4_out), .in1(3'b100), .out(multiplexer_6_out), .sel(is_J_type));
  or or_4 (ASel, is_auipc, is_B_type, is_J_type);
  Multiplexer #(.enable("false"), .width(4)) multiplexer_7 (
    .in0(multiplexer_5_out), .in1(4'b1010), .out(multiplexer_7_out), .sel(is_mul));
  Multiplexer #(.enable("false"), .width(2)) multiplexer_8 (
    .in0(2'b01), .in1(2'b00), .out(multiplexer_8_out), .sel(is_load_inst));
  Comparator #(.width(3)) comparator_20 (.a(inst[14:12]), .b(3'b101), .eq(comparator_20_eq));  // open: gt, lt
  Multiplexer #(.enable("false"), .width(3)) multiplexer_9 (
    .in0(multiplexer_6_out), .in1(3'b101), .out(ImmSel), .sel(CSRWen));
  Multiplexer #(.enable("false"), .width(4)) multiplexer_10 (
    .in0(multiplexer_7_out), .in1(4'b1110), .out(multiplexer_10_out), .sel(is_mulh));
  and and_10 (CSRSel, comparator_20_eq, CSRWen);
  and and_11 (and_11_out, is_B_type, or_3_out);
  Multiplexer #(.enable("false"), .width(4)) multiplexer_11 (
    .in0(multiplexer_10_out), .in1(4'b0101), .out(multiplexer_11_out), .sel(is_sra_or_srai));
  Multiplexer #(.enable("false"), .width(2)) multiplexer_12 (
    .in0(multiplexer_8_out), .in1(2'b10), .out(WBSel), .sel(or_5_out));
  or or_5 (or_5_out, is_jalr, is_J_type);
  or or_6 (PCSel, is_J_type, and_11_out, is_jalr);
  Comparator #(.width(3)) comparator_21 (.a(inst[14:12]), .b(3'b101), .eq(comparator_21_eq));  // open: gt, lt
  Comparator #(.width(7)) comparator_22 (.a(inst[31:25]), .b(7'b0100000), .eq(comparator_22_eq));  // open: gt, lt
  or or_7 (or_7_out, is_R_type, is_I_type);
  Comparator #(.width(7)) comparator_23 (.a(inst[6:0]), .b(7'b0010011), .eq(comparator_23_eq));  // open: gt, lt
  and and_12 (is_sra_or_srai, comparator_21_eq, comparator_22_eq, or_7_out);
  Multiplexer #(.enable("false"), .width(4)) multiplexer_13 (
    .in0(4'b0000), .in1(multiplexer_11_out), .out(ALUSel), .sel(or_8_out));
  or or_8 (or_8_out, comparator_23_eq, is_R_type);
  Comparator #(.width(7)) comparator_24 (.a(inst[6:0]), .b(7'b0010111), .eq(is_auipc));  // open: gt, lt
  Comparator #(.width(7)) comparator_25 (.a(inst[6:0]), .b(7'b0110111), .eq(is_lui));  // open: gt, lt
  Comparator #(.width(7)) comparator_26 (.a(inst[6:0]), .b(7'b1101111), .eq(is_J_type));  // open: gt, lt
  Comparator #(.width(7)) comparator_27 (.a(inst[6:0]), .b(7'b1100111), .eq(is_jalr));  // open: gt, lt
  Comparator #(.width(7)) comparator_28 (.a(inst[6:0]), .b(7'b1110011), .eq(CSRWen));  // open: gt, lt
  or or_9 (BrUn, is_bltu, is_bgeu);
  or or_10 (BSel, is_I_type, is_B_type, is_U_type, is_J_type, is_jalr);
  or or_11 (is_U_type, is_auipc, is_lui);
  or or_12 (RegWEn, is_R_type, is_I_type, is_auipc, is_lui, is_J_type, is_jalr);

  // Other names for the same wires on the sheet: ALU_operation_code[3:0] = ALUSel; immediate_type[2:0] = ImmSel;
  //   opcode[6:0] = inst[6:0]; rd[4:0] = inst[11:7]; funct3[2:0] = inst[14:12]; rs1[4:0] = inst[19:15];
  //   rs2[4:0] = inst[24:20]; funct7[6:0] = inst[31:25]; is_branch_unsigned = BrUn; is_CSR = CSRWen;
  //   is_jal = is_J_type; is_operand_A_the_PC = ASel; is_operand_B_an_immediate = BSel; is_S_type = MemRW;
  //   reg_write_back_selection[1:0] = WBSel; should_branch = PCSel; should_write_back_reg = RegWEn

  // Notes on the sheet:
  //   INPUTS to your circuit
  //   DON'T CHANGE THE LOCATIONS OF THE INPUTS AND OUTPUTS!
  //   OUTPUT from your circuit
endmodule
