// Logisim project cpu.circ as structural Verilog: 1 circuit, main circuit cpu
module cpu (
  input  clk,
  input  [31:0] INSTRUCTION,
  input  [31:0] READ_DATA,
  output [31:0] WRITE_ADDRESS,
  output [31:0] PROGRAM_COUNTER,
  output [31:0] ra,
  output [31:0] sp,
  output [31:0] t0,
  output [31:0] t1,
  output [31:0] t2,
  output [31:0] s0,
  output [31:0] s1,
  output [31:0] a0,
  output [31:0] tohost,
  output [3:0] WRITE_ENABLE,
  output [31:0] WRITE_DATA
);

  wire ASel, BrEq, BrLt, BrUn, BSel, comparator_1_eq, comparator_2_eq, comparator_3_eq, comparator_4_eq,
       comparator_5_eq, comparator_6_eq, comparator_7_eq, comparator_8_eq, CSRSel, CSRWen, is_lb_out,
       is_lh_out, is_sb_out, is_sh_out, MemRW, PCSel, RegWEn;
  wire [1:0] WBSel;
  wire [2:0] funct3, ImmSel;
  wire [3:0] ALUSel, multiplexer_4_out, multiplexer_7_out;
  wire [31:0] adder_1_out, adder_2_out, HANDELED_READ_DATA, Imm, INSTRUCTION_2, multiplexer_1_out,
       multiplexer_2_out, multiplexer_3_out, multiplexer_5_out, multiplexer_6_out, multiplexer_9_out,
       PROGRAM_COUNTER_2, READ_DATA_8b, READ_DATA_16b, Reg_Write_Data, regfile_1_read_data_1;

  Adder #(.width(32)) adder_1 (.a(PROGRAM_COUNTER), .b(32'h4), .out(adder_1_out));  // open: cin, cout
  Multiplexer #(.enable("false"), .width(32)) multiplexer_1 (
    .in0(adder_1_out), .in1(WRITE_ADDRESS), .out(multiplexer_1_out), .sel(PCSel));
  Register #(.width(32)) register_1 (.D(PROGRAM_COUNTER), .clk(clk), .Q(PROGRAM_COUNTER_2));  // open: en, clr
  Register #(.width(32)) register_2 (
    .D(multiplexer_2_out), .clk(clk), .Q({INSTRUCTION_2[31:15], funct3, INSTRUCTION_2[11:0]}));  // open: en, clr
  Multiplexer #(.enable("false"), .width(32)) multiplexer_2 (
    .in0(INSTRUCTION), .in1(32'h13), .out(multiplexer_2_out), .sel(PCSel));
  control_logic control_logic_1 (
    .CSRWen(CSRWen), .PCSel(PCSel), .RegWEn(RegWEn), .ImmSel(ImmSel), .BrUn(BrUn), .ASel(ASel), .BSel(BSel),
    .ALUSel(ALUSel), .MemRW(MemRW), .WBSel(WBSel), .CSRSel(CSRSel),
    .inst({INSTRUCTION_2[31:15], funct3, INSTRUCTION_2[11:0]}), .BrEq(BrEq), .BrLt(BrLt));
  Register #(.width(32)) PC (.D(multiplexer_1_out), .clk(clk), .Q(PROGRAM_COUNTER));  // open: en, clr
  imm_gen imm_gen_1 (.inst({INSTRUCTION_2[31:15], funct3, INSTRUCTION_2[11:0]}), .ImmSel(ImmSel), .imm(Imm));
  regfile regfile_1 (
    .rs1(INSTRUCTION_2[19:15]), .rs2(INSTRUCTION_2[24:20]), .rd(INSTRUCTION_2[11:7]),
    .Write_Data(Reg_Write_Data), .RegWEn(RegWEn), .clk(clk), .ra(ra), .sp(sp), .t0(t0), .t1(t1), .t2(t2),
    .s0(s0), .s1(s1), .a0(a0), .Read_Data_1(regfile_1_read_data_1), .Read_Data_2(WRITE_DATA));
  Multiplexer #(.enable("false"), .width(32)) multiplexer_3 (
    .in0(regfile_1_read_data_1), .in1(Imm), .out(multiplexer_3_out), .sel(CSRSel));
  assign READ_DATA_8b = {{24{READ_DATA[7]}}, READ_DATA[7:0]};  // Bit_Extender bit_extender_1
  assign READ_DATA_16b = {{16{READ_DATA[15]}}, READ_DATA[15:0]};  // Bit_Extender bit_extender_2
  Comparator #(.width(7)) comparator_1 (.a(INSTRUCTION_2[6:0]), .b(7'b0100011), .eq(comparator_1_eq));  // open: gt, lt
  Comparator #(.width(3)) comparator_2 (.a(funct3), .b(3'b001), .eq(comparator_2_eq));  // open: gt, lt
  branch_comp branch_comp_1 (.rs1(regfile_1_read_data_1), .rs2(WRITE_DATA), .BrUn(BrUn), .BrEq(BrEq), .BrLt(BrLt));
  csr csr_1 (.CSR_address(12'h51e), .CSR_din(multiplexer_3_out), .CSR_WE(CSRWen), .clk(clk), .tohost(tohost));
  Multiplexer #(.enable("false"), .width(4)) multiplexer_4 (
    .in0(4'b1111), .in1(4'b0011), .out(multiplexer_4_out), .sel(is_sh_out));
  and is_sh (is_sh_out, comparator_1_eq, comparator_2_eq);
  Comparator #(.width(7)) comparator_3 (.a(INSTRUCTION_2[6:0]), .b(7'b0100011), .eq(comparator_3_eq));  // open: gt, lt
  Comparator #(.width(3)) comparator_4 (.a(funct3), .b(3'b000), .eq(comparator_4_eq));  // open: gt, lt
  Multiplexer #(.enable("false"), .width(32)) multiplexer_5 (
    .in0(regfile_1_read_data_1), .in1(PROGRAM_COUNTER_2), .out(multiplexer_5_out), .sel(ASel));
  Multiplexer #(.enable("false"), .width(32)) multiplexer_6 (
    .in0(WRITE_DATA), .in1(Imm), .out(multiplexer_6_out), .sel(BSel));
  Multiplexer #(.enable("false"), .width(4)) multiplexer_7 (
    .in0(multiplexer_4_out), .in1(4'b0001), .out(multiplexer_7_out), .sel(is_sb_out));
  and is_sb (is_sb_out, comparator_3_eq, comparator_4_eq);
  Comparator #(.width(7)) comparator_5 (.a(INSTRUCTION_2[6:0]), .b(7'b0000011), .eq(comparator_5_eq));  // open: gt, lt
  Comparator #(.width(3)) comparator_6 (.a(funct3), .b(3'b001), .eq(comparator_6_eq));  // open: gt, lt
  Multiplexer #(.enable("false"), .width(4)) multiplexer_8 (
    .in0(4'b0000), .in1(multiplexer_7_out), .out(WRITE_ENABLE), .sel(MemRW));
  alu alu_1 (.Result(WRITE_ADDRESS), .A(multiplexer_5_out), .B(multiplexer_6_out), .ALUSel(ALUSel));
  Multiplexer #(.enable("false"), .width(32)) multiplexer_9 (
    .in0(READ_DATA), .in1(READ_DATA_16b), .out(multiplexer_9_out), .sel(is_lh_out));
  and is_lh (is_lh_out, comparator_5_eq, comparator_6_eq);
  Comparator #(.width(7)) comparator_7 (.a(INSTRUCTION_2[6:0]), .b(7'b0000011), .eq(comparator_7_eq));  // open: gt, lt
  and is_lb (is_lb_out, comparator_7_eq, comparator_8_eq);
  Comparator #(.width(3)) comparator_8 (.a(funct3), .b(3'b000), .eq(comparator_8_eq));  // open: gt, lt
  Multiplexer #(.enable("false"), .width(32)) multiplexer_10 (
    .in0(multiplexer_9_out), .in1(READ_DATA_8b), .out(HANDELED_READ_DATA), .sel(is_lb_out));
  Adder #(.width(32)) adder_2 (.a(PROGRAM_COUNTER_2), .b(32'h4), .out(adder_2_out));  // open: cin, cout
  Multiplexer #(.enable("false"), .select(2), .width(32)) multiplexer_11 (
    .in0(HANDELED_READ_DATA), .in1(WRITE_ADDRESS), .in2(adder_2_out), .in3(Imm), .out(Reg_Write_Data),
    .sel(WBSel));

  // Other names for the same wires on the sheet: ALU_RES[31:0] = WRITE_ADDRESS; opcode[6:0] = INSTRUCTION_2[6:0];
  //   rd[4:0] = INSTRUCTION_2[11:7]; INSTRUCTION_2[14:12] = funct3; rs1[4:0] = INSTRUCTION_2[19:15];
  //   rs2[4:0] = INSTRUCTION_2[24:20]

  // Notes on the sheet:
  //   Output to IMEM
  //   IMEM (do **NOT** move this)
  //   Inputs from IMEM
  //   It is OK to move the PC, RegFile, ALU, MEM, Branch Comp, Imm Gen, and Control Logic to wherever is most convenient for you when constructing your CPU, and to delete this text
  //   Inputs/Outputs for testing. Do **NOT** move these.
  //   Outputs To DMEM
  //   DMEM (do **NOT** move this)
  //   Inputs From DMEM
endmodule
